# Fritzing sketch zynthian_2in1 (saved by Fritzing 0.9.2b)
circuit board: 5.24017cm x 1.76117cm
breadboards: 1

parts:
  R1 = Resistor [tolerance=±5% resistance=1k package=THT]
  R2 = Resistor [tolerance=±5% resistance=10k package=THT]
  D1 = Rectifier Diode [part_number=1N4148 package="300 mil [THT]"]
  R3 = Resistor [tolerance=±5% resistance=220 package=THT]
  MIDI-IN = Header 2 [package=molex-1x2_lock]
  C1 = Ceramic Capacitor [capacitance=100nF package="100 mil [THT, multilayer]"]
  C2 = Ceramic Capacitor [capacitance=100nF package="100 mil [THT, multilayer]"]
  6N138 = 6N138 [package="DIP (Dual Inline) [THT]"]
  MCP23008 = Microchip MCP23008 8-bit I/O expander [part_number=MCP23008 package="DIP (Dual Inline) [THT]"]
  GPIO-ext = male pin header, 8 pins [form="♂ (male)"]
  RBPi = male pin header, 6 pins [form="♂ (male)"]

nets:
  N1: R1.Pin_0, 6N138.Output, RBPi.pin2
  N2: R1.Pin_1, C2.1, 6N138.Vcc, RBPi.pin1
  N3: R2.Pin_0, 6N138.Output_Base
  GND: R2.Pin_1, C1.1, C2.0, 6N138.GND, MCP23008.A2, MCP23008.A1, MCP23008.A0, MCP23008.VSS, RBPi.pin6
  N4: D1.cathode, R3.Pin_1, 6N138.Anode
  N5: D1.anode, MIDI-IN.2, 6N138.Cathode
  N6: R3.Pin_0, MIDI-IN.1
  N7: C1.0, MCP23008.Reset, MCP23008.VDD, RBPi.pin5
  N8: MCP23008.SCL, RBPi.pin4
  N9: MCP23008.SDA, RBPi.pin3
  N10: MCP23008.GP0, GPIO-ext.pin1
  N11: MCP23008.GP1, GPIO-ext.pin2
  N12: MCP23008.GP2, GPIO-ext.pin3
  N13: MCP23008.GP3, GPIO-ext.pin4
  N14: MCP23008.GP4, GPIO-ext.pin5
  N15: MCP23008.GP5, GPIO-ext.pin6
  N16: MCP23008.GP6, GPIO-ext.pin7
  N17: MCP23008.GP7, GPIO-ext.pin8

custom parts:
  6N138: Optocoupler
  Microchip MCP23008 8-bit I/O expander: Provides 8-bit, general purpose, parallel I/O expansion for I2C bus. Datasheet: http://ww1.microchip.com/downloads/en/devicedoc/21919e.pdf
