# Fritzing sketch zynthian_controller (saved by Fritzing 0.8.7b)
circuit board: 1.8cm x 6.25cm
breadboards: 1

parts:
  ENC1 = Rotary Encoder with Knob
  ENC2 = Rotary Encoder with Knob
  RBPi = Header 6 [package=molex-1x6_lock]
  C1 = Ceramic Capacitor [capacitance=100nF package="100 mil [THT, multilayer]"]
  C2 = Ceramic Capacitor [capacitance=100nF package="100 mil [THT, multilayer]"]
  SW2 = Header 2 [package=molex-1x2_lock]

nets:
  N1: ENC1.no_name_yet#1, RBPi.1
  GND: ENC1.no_name_yet#2, ENC1.no_name_yet#5, ENC2.no_name_yet#2, ENC2.no_name_yet#5, RBPi.6, C1.0, C2.1, SW2.1
  N2: ENC1.no_name_yet#3, RBPi.2
  N3: ENC1.no_name_yet#4, RBPi.3, C1.1
  N4: ENC2.no_name_yet#1, RBPi.4
  N5: ENC2.no_name_yet#3, RBPi.5
  N6: ENC2.no_name_yet#4, C2.0, SW2.2

custom parts:
  Rotary Encoder with Knob: Rotary Encoder with 1/4" Shaft and Knob
