# Fritzing sketch zynthian_controller_old (saved by Fritzing 0.8.7b)
circuit board: 1.8cm x 6.25cm
breadboards: 1

parts:
  ENCODER1 = Rotary Encoder with Knob
  ENCODER2 = Rotary Encoder with Knob
  Head-6 = Header 6 [package=molex-1x6_lock]

nets:
  N1: ENCODER1.no_name_yet#1, Head-6.1
  GND: ENCODER1.no_name_yet#2, ENCODER1.no_name_yet#5, ENCODER2.no_name_yet#2, ENCODER2.no_name_yet#5, Head-6.6
  N2: ENCODER1.no_name_yet#3, Head-6.2
  N3: ENCODER1.no_name_yet#4, Head-6.3
  N4: ENCODER2.no_name_yet#1, Head-6.4
  N5: ENCODER2.no_name_yet#3, Head-6.5

custom parts:
  Rotary Encoder with Knob: Rotary Encoder with 1/4" Shaft and Knob
