# Fritzing sketch zynthian_midi (saved by Fritzing 0.8.7b)
circuit board: 4.04391cm x 1.62678cm
breadboards: 1

parts:
  JP1 = Header 6 [package=molex-1x6_lock]
  R2 = Resistor [tolerance=±5% resistance=1k package=THT]
  R3 = Resistor [tolerance=±5% resistance=10k package=THT]
  C1 = Ceramic Capacitor [capacitance=100nF package="100 mil [THT, multilayer]"]
  D1 = Rectifier Diode [part_number=1N4148 package="300 mil [THT]"]
  R4 = Resistor [tolerance=±5% resistance=220 package=THT]
  6N138 = OPTO_DARL_6N138 [package=8-dip]

nets:
  N1: JP1.1, R2.Pin_1, C1.0, 6N138.VCC
  N2: JP1.2, R3.Pin_0, C1.1, 6N138.GND
  N3: JP1.3, D1.anode, 6N138.C
  N4: JP1.4, R4.Pin_0
  N5: JP1.5, R2.Pin_0, 6N138.VOUT
  N6: R3.Pin_1, 6N138.BR
  N7: D1.cathode, R4.Pin_1, 6N138.A

custom parts:
  OPTO_DARL_6N138: Optoisolator, darlington pair output
