# Fritzing sketch wiring_scheme_controllers (saved by Fritzing 0.9.2b)

parts:
  J2 = female pin header, 6 pins [form="♀ (female)"]
  J1 = shrouded pin header, 40 pins [form="♂ (shrouded male)"]
  J3 = female pin header, 6 pins [form="♀ (female)"]
  J4 = female pin header, 2 pins [form="♀ (female)"]
  J5 = female pin header, 2 pins [form="♀ (female)"]
  J6 = longpad pin header, 8 pins [form="long pad"]

nets:
  N1: J2.pin1, J1.pin33
  N2: J2.pin2, J1.pin8
  N3: J2.pin3, J1.pin7
  N4: J2.pin4, J1.pin6
  N5: J2.pin5, J1.pin4
  N6: J2.pin6, J1.pin34
  N7: J1.pin15, J3.pin5
  N8: J1.pin17, J3.pin3
  N9: J1.pin19, J3.pin1
  N10: J1.pin23, J3.pin2
  N11: J1.pin25, J3.pin4
  N12: J1.pin26, J3.pin6
  N13: J4.pin2, J6.pin8
  N14: J5.pin2, J6.pin7

notes:
  Controller 2
  Mail main-ribbon cable connector
  pin1
  pin2
  pin40
  Controller 1
  2in1
