# Fritzing sketch wiring_scheme_2in1 (saved by Fritzing 0.9.2b)

parts:
  J2 = female pin header, 6 pins [form="♀ (female)"]
  J1 = shrouded pin header, 40 pins [form="♂ (shrouded male)"]

nets:
  N1: J2.pin1, J1.pin1
  N2: J2.pin2, J1.pin36
  N3: J2.pin3, J1.pin2
  N4: J2.pin4, J1.pin3
  N5: J2.pin5, J1.pin40
  N6: J2.pin6, J1.pin38

notes:
  2in1
  Main-ribbon cable connector
  pin1
  pin2
  pin40
