# Fritzing sketch wiring_scheme_controllers_single_alt (saved by Fritzing 0.9.2b)

parts:
  J1 = shrouded pin header, 40 pins [form="♂ (shrouded male)"]
  J6 = longpad pin header, 8 pins [form="long pad"]
  J2 = female pin header, 4 pins [form="♀ (female)"]
  J7 = female pin header, 4 pins [form="♀ (female)"]
  J8 = female pin header, 4 pins [form="♀ (female)"]
  J9 = female pin header, 4 pins [form="♀ (female)"]

nets:
  N1: J1.pin4, J2.pin2
  N2: J1.pin5, J2.pin4
  N3: J1.pin6, J2.pin1
  N4: J1.pin8, J7.pin2
  N5: J1.pin15, J8.pin2
  N6: J1.pin19, J9.pin1
  N7: J1.pin23, J9.pin2
  N8: J1.pin24, J9.pin4
  N9: J1.pin25, J8.pin1
  N10: J1.pin26, J8.pin4
  N11: J1.pin33, J7.pin1
  N12: J1.pin34, J7.pin4
  N13: J6.pin5, J7.pin3
  N14: J6.pin6, J9.pin3
  N15: J6.pin7, J2.pin3
  N16: J6.pin8, J8.pin3

notes:
  Controller 3
  Main-ribbon cable connector
  pin1
  pin2
  pin40
  2in1
  Controller 4
  Controller 1
  Controller 2
  pin7
  pin8
  (MCP23008)
  pin6
  pin5
