# Fritzing sketch zynthian_controller_single (saved by Fritzing 0.9.2b)
circuit board: 1.83985cm x 2.72124cm
breadboards: 1

parts:
  ENC1 = Rotary Encoder with Knob
  C1 = Ceramic Capacitor [capacitance=100nF package="100 mil [THT, multilayer]"]
  RBPi = Header 4 [package=molex-1x4_lock]
  C2 = Ceramic Capacitor [capacitance=100nF package="100 mil [THT, multilayer]"]
  C3 = Ceramic Capacitor [capacitance=100nF package="100 mil [THT, multilayer]"]

nets:
  N1: ENC1.no_name_yet#1, RBPi.4, C2.0
  GND: ENC1.no_name_yet#2, ENC1.no_name_yet#5, C1.1, RBPi.1, C2.1, C3.0
  N2: ENC1.no_name_yet#3, RBPi.3, C3.1
  N3: ENC1.no_name_yet#4, C1.0, RBPi.2

custom parts:
  Rotary Encoder with Knob: Rotary Encoder with 1/4" Shaft and Knob
